// Logisim project FelipeRezende.circ as structural Verilog
module Meio_Somador (
  input  A,
  input  B,
  output S,
  output S_2
);

  xor xor_1 (S, A, B);
  and and_1 (S_2, A, B);
endmodule
